// Logisim project AddandSub.circ as structural Verilog: 1 circuit, main circuit main
module main (
  input  in_1,
  input  HALF_ADDER,
  input  in_3,
  input  in_4,
  input  FULL_ADDER,
  input  in_6,
  input  in_7,
  input  in_8,
  input  in_9,
  input  in_10
);

  wire and_1_out, and_2_out, and_3_out, and_4_out, and_5_out, and_6_out, and_7_out, not_1_out, not_3_out,
       xor_1_out, xor_2_out, xor_3_out, xor_4_out, xor_5_out, xor_6_out, xor_7_out;

  xor xor_1 (xor_1_out, HALF_ADDER, in_4);
  and and_1 (and_1_out, HALF_ADDER, in_4);
  xor xor_2 (xor_2_out, FULL_ADDER, in_7);
  and and_2 (and_2_out, FULL_ADDER, in_7);
  LED led_1 (.in(xor_1_out));
  LED led_2 (.in(and_1_out));
  xor xor_3 (xor_3_out, xor_2_out, in_8);
  and and_3 (and_3_out, in_8, and_2_out);
  LED led_3 (.in(xor_3_out));
  LED led_4 (.in(and_3_out));
  not not_1 (not_1_out, in_1);
  LED led_5 (.in(xor_4_out));
  xor xor_4 (xor_4_out, in_1, in_3);
  and and_4 (and_4_out, not_1_out, in_3);
  LED led_6 (.in(and_4_out));
  xor xor_5 (xor_5_out, in_6, in_9);
  not not_2 (in_10, in_6);
  not not_3 (not_3_out, in_6);
  and and_5 (and_5_out, in_10, in_9);
  and and_6 (and_6_out, in_10, in_9);
  and and_7 (and_7_out, not_3_out, in_10);
  xor xor_6 (xor_6_out, xor_5_out, in_10);
  LED led_7 (.in(xor_6_out));
  ExactlyOne xor_7 (.out(xor_7_out), .in0(and_5_out), .in1(and_6_out), .in2(and_7_out));
  LED led_8 (.in(xor_7_out));

  // Notes on the sheet:
  //   HALF SUBTRACTOR
  //   FULL SUBTRACTOR
endmodule
