// Logisim project EncodandDecode.circ as structural Verilog: 1 circuit, main circuit main
module main (
  input  D0,
  input  D1,
  input  D2,
  input  D3,
  input  D4,
  input  D5,
  input  D7,
  input  in_8,
  input  in_9,
  input  in_10,
  input  in_11,
  output out_12,
  output out_13,
  output out_14,
  output out_15,
  output out_16,
  output out_17,
  output out_18,
  output out_19,
  output out_20,
  output out_21,
  output out_22
);

  wire not_1_out, not_2_out, not_3_out, undriven, undriven_2, undriven_3, undriven_4, undriven_5, undriven_6,
       undriven_7;

  not not_1 (not_1_out, in_9);
  not not_2 (not_2_out, in_10);
  not not_3 (not_3_out, in_11);
  or or_1 (out_12, undriven_4, undriven_5, undriven_6, undriven_7);
  or or_2 (out_13, undriven_2, undriven_3, undriven_6, undriven_7);
  or or_3 (out_14, undriven, undriven_3, undriven_5, undriven_7);
  or or_4 (out_15, not_3_out, not_2_out, not_1_out);
  or or_5 (out_16, in_11, not_2_out, not_1_out);
  or or_6 (out_17, not_3_out, not_2_out, not_1_out);
  or or_7 (out_18, in_11, in_10, not_1_out);
  or or_8 (out_19, not_3_out, not_2_out, in_9);
  or or_9 (out_20, in_11, not_2_out, in_9);
  or or_10 (out_21, not_3_out, in_10, in_9);
  or or_11 (out_22, in_11, in_10, in_9);

  // Notes on the sheet:
  //   DECODER
  //   ENCODER
  //   D6
endmodule
