// Logisim project MuxandDemux.circ as structural Verilog: 1 circuit, main circuit main
module main (
  input  in_1,
  input  in_2,
  input  in_3,
  input  in_4,
  input  in_5,
  input  in_6,
  input  in_7,
  input  in_8,
  input  in_9,
  output out_10,
  output out_11,
  output out_12,
  output out_13,
  output out_14
);

  wire and_1_out, and_2_out, and_3_out, and_4_out, not_1_out, not_2_out, not_3_out, not_4_out;

  not not_1 (not_1_out, in_6);
  not not_2 (not_2_out, in_8);
  and and_1 (and_1_out, in_1, in_6, in_8);
  and and_2 (and_2_out, in_2, not_1_out, in_8);
  and and_3 (and_3_out, in_3, in_6, not_2_out);
  and and_4 (and_4_out, in_5, not_1_out, not_2_out);
  nor nor_1 (out_12, and_1_out, and_2_out, and_3_out, and_4_out);
  not not_3 (not_3_out, in_7);
  not not_4 (not_4_out, in_9);
  and and_5 (out_10, in_4, in_7, in_9);
  and and_6 (out_11, in_4, not_3_out, in_9);
  and and_7 (out_13, in_4, in_7, not_4_out);
  and and_8 (out_14, in_4, not_3_out, not_4_out);

  // Notes on the sheet:
  //   MULTIPLEXER
  //   DEMULTIPLEXER
endmodule
